# Fritzing sketch Project_04 (saved by Fritzing 0.6.3b)
breadboards: 1

parts:
  Arduino_ADK = Arduino Mega
  R1 = Trimmer Potentiometer [maximum_resistance=100kΩ package=THT]

nets:
  N1: Arduino_ADK.GND, R1.leg1
  N2: Arduino_ADK.+5V, R1.leg2
  N3: Arduino_ADK.A0, R1.wiper
