# Fritzing sketch Project_07 (saved by Fritzing 0.6.3b)
breadboards: 1

parts:
  Arduino_Mega_ADK = Arduino Mega
  R1 = Photocell (LDR) [package=THT]
  R2 = Resistor [tolerance=±5% resistance=10k package=THT]

nets:
  N1: Arduino_Mega_ADK.+5V, R1.pin_0
  N2: Arduino_Mega_ADK.GND, R2.Pin_1
  N3: Arduino_Mega_ADK.A0, R1.pin_1, R2.Pin_0
