# Fritzing sketch Project_08 (saved by Fritzing 0.6.3b)
breadboards: 1

parts:
  Arduino_Mega_ADK = Arduino Mega
  R1 = Resistor [tolerance=±5% resistance=10k package=THT]
  T1 = Temperature Sensor (Thermistor) [thermistor_type=NTC package=THT]

nets:
  N1: Arduino_Mega_ADK.+5V, T1.pin_0
  N2: Arduino_Mega_ADK.GND, R1.Pin_1
  N3: Arduino_Mega_ADK.A0, R1.Pin_0, T1.pin_1
