# Fritzing sketch Project_09 (saved by Fritzing 0.6.3b)
breadboards: 1

parts:
  Arduino_Mega_ADK = Arduino Mega
  R1 = Resistor [tolerance=±5% resistance=10k package=THT]
  Capacitive_Touch_Sensor = female pin header, 1 pin [form="♀ (female)"]

nets:
  N1: Arduino_Mega_ADK.D6, R1.Pin_0, Capacitive_Touch_Sensor.pin1
  N2: Arduino_Mega_ADK.D4, R1.Pin_1
