# Fritzing sketch Project_11_external_battery (saved by Fritzing 0.6.3b)
breadboards: 1

parts:
  Arduino_ADK = Arduino Mega
  M1 = DC Motor
  T1 = NPN-Transistor [package="TO92 [THT]"]
  VCC1 = Battery block 9V
  R1 = Resistor [tolerance=±5% resistance=1k package=THT]

nets:
  N1: Arduino_ADK.D2, R1.Pin_0
  N2: Arduino_ADK.GND, T1.E, VCC1.-
  N3: M1.pin_1, T1.C
  N4: M1.pin_2, VCC1.+
  N5: T1.B, R1.Pin_1
