# Fritzing sketch Project_12_Piezo_Buzzer_Circuit (saved by Fritzing 0.6.3b)
breadboards: 1

parts:
  Arduino_ADK = Arduino Mega
  J1 = Piezo Speaker

nets:
  N1: Arduino_ADK.D3, J1.pin2
  N2: Arduino_ADK.GND, J1.pin1
