# Fritzing sketch Project_12_Tilt_Switch_Circuit (saved by Fritzing 0.6.3b)
breadboards: 1

parts:
  Arduino_ADK = Arduino Mega
  S2 = Tilt Switch [package=THT]
  R3 = Resistor [tolerance=±5% resistance=10k package=THT]

nets:
  N1: Arduino_ADK.D5, S2.Pin_2, R3.Pin_1
  N2: Arduino_ADK.+5V, R3.Pin_0
  N3: Arduino_ADK.GND, S2.Pin_1
